// Logisim project digital lock.circ as structural Verilog: 1 circuit, main circuit main
module main (
  input  [3:0] PASSWORD_INPUT,
  input  [3:0] USER_INPUT,
  output out_3
);

  wire comparator_1_eq, comparator_1_gt, comparator_1_lt, comparator_2_eq, comparator_2_gt, comparator_2_lt,
       comparator_3_eq, comparator_3_gt, comparator_3_lt, or_1_out, or_2_out, RESET_ALL_out, SET_PASSWORD_out;
  wire [3:0] REGISTER_2_q, REGISTER_3_q, REGISTER_q;

  Button SET_PASSWORD (.out(SET_PASSWORD_out));
  Button RESET_ALL (.out(RESET_ALL_out));
  Register #(.width(4)) REGISTER (
    .D(PASSWORD_INPUT), .Q(REGISTER_q), .clk(SET_PASSWORD_out), .clr(RESET_ALL_out));  // open: en
  Register #(.width(4)) REGISTER_2 (
    .D(REGISTER_q), .Q(REGISTER_2_q), .clk(SET_PASSWORD_out), .clr(RESET_ALL_out));  // open: en
  Register #(.width(4)) REGISTER_3 (.D(REGISTER_2_q), .Q(REGISTER_3_q), .clk(SET_PASSWORD_out));  // open: en, clr
  Comparator #(.width(4)) comparator_1 (
    .a(REGISTER_2_q), .b(USER_INPUT), .gt(comparator_1_gt), .eq(comparator_1_eq), .lt(comparator_1_lt));
  Comparator #(.width(4)) comparator_2 (
    .a(REGISTER_3_q), .b(USER_INPUT), .gt(comparator_2_gt), .eq(comparator_2_eq), .lt(comparator_2_lt));
  Comparator #(.width(4)) comparator_3 (
    .a(REGISTER_q), .b(USER_INPUT), .gt(comparator_3_gt), .eq(comparator_3_eq), .lt(comparator_3_lt));
  Counter #(.max('h3)) counter_1 (.carry(out_3), .clk(or_1_out), .clr(RESET_ALL_out));  // open: load, D, count, Q
  or or_1 (or_1_out, comparator_1_gt, comparator_1_lt, comparator_2_gt, comparator_2_lt, comparator_3_gt, comparator_3_lt);
  LED led_1 (.in(or_2_out));
  or or_2 (or_2_out, comparator_3_eq, comparator_1_eq, comparator_2_eq);
  LED led_2 (.in(or_1_out));

  // Notes on the sheet:
  //   3 BIT MAGNITUDE COMPARATOR 
  //   PASSWORD MATCHED
  //   Wrong Password
endmodule
